# Fritzing sketch ESP8266 Arduboy (saved by Fritzing 0.9.3b)
breadboards: 2

parts:
  WeMos_D1_Mini3 = WeMos D1 Mini  # not connected
  LED1 = LED - 3mm [color="Red (633nm)" package="3 mm [THT]"]
  LED2 = LED - 3mm [color="Yellow (592nm)" package="3 mm [THT]"]
  R1 = Resistor [tolerance=±5% resistance=220 package="0603 [SMD]"]
  U1 = SIP - 4 pins [part_number=SHT20 chip_label=SHT20 package="SIP (Single Inline) [THT]"]
  R2 = Resistor [tolerance=±5% resistance=1k package="0603 [SMD]"]
  Piezo1 = Piezo Speaker - PC Mount [part_number=COM-07950]
  SW = IC, DIP package, 4 pins [chip_label=U]
  IC1 = DIP - 4 pins [chip_label=L package="DIP (Dual Inline) [THT]"]
  IC2 = DIP - 4 pins [chip_label=R package="DIP (Dual Inline) [THT]"]
  IC3 = DIP - 4 pins [chip_label=D package="DIP (Dual Inline) [THT]"]
  IC4 = DIP - 4 pins [chip_label=A package="DIP (Dual Inline) [THT]"]
  IC5 = DIP - 4 pins [chip_label=B package="DIP (Dual Inline) [THT]"]
  LED3 = LED - 3mm [color="Green (565nm)" package="3 mm [THT]"]
  R3 = Resistor [tolerance=±5% resistance=470 package="0603 [SMD]"]
  Squix1 = OLED 0.96" 128x64 I2C SSD1306 (GND/VCC)
  R4 = Resistor [tolerance=±5% resistance=10k package=THT]
  Paddle = Trimmer Potentiometer [maximum_resistance=10kΩ package=THT]

nets:
  N1: LED1.cathode, IC1.pin4
  N2: LED2.cathode, SW.pin1, SW.pin4
  N3: LED2.anode, R3.Pin_0
  N4: R1.Pin_0, LED3.anode
  VCC: R1.Pin_1, U1.VCC, R2.Pin_1, R3.Pin_1, Squix1.VCC, R4.Pin_0, Paddle.leg2
  N5: U1.SDA, Squix1.SCL
  N6: U1.SCL, Squix1.SCA
  GND: U1.GND, Piezo1.GND, SW.pin2, SW.pin3, Squix1.GND, Paddle.leg1
  N7: IC1.pin2, IC2.pin2, IC3.pin2, IC3.pin3, IC4.pin1, IC4.pin4, IC5.pin1, IC5.pin4
  N8: IC2.pin4, LED3.cathode
  N9: IC3.pin1, IC3.pin4
  N10: IC4.pin2, IC4.pin3
  N11: IC5.pin2, IC5.pin3, R4.Pin_1

notes:
  V S S G
  C D C N
  C A L D
  1K, 470, 220
  Resistors
  10K Resistor
  Game 8266 Micropython game console I2C version
  cheungbx 2019-09-17
  pin layout for
  Node MCU D1 Mini
  GPIO13 D7------ Right
  GPIO12 D6—— Left
  GPIO14 D5—— UP
  GPIO2 D4—— Down
  GPIO0 D3—— A
  GPIO16 D0 —— B (connect 10K pullup resistor to 3.3V)
  GPIO15 D8—— Speaker
  *Tie the other end of the buttons to GND
  # I2C OLED
  # SSD1306 # ESP8266
  # GND -------- GND
  # VCC --------- VCC
  # D0/SCL ------ D1 (=GPIO5)
  # D1/SDA ---- D2 (=GPIO4)
  # Speaker+ -- D8 -(GPIO15)
  # Speaker- ---GND
  # Paddle, connect a 10K V.R.
  # ADC (0) - A0

custom parts:
  SIP - 4 pins: A SIP stand-in part for whatever you want. With 4 pins on a 300 mil single inline package (SIP) footprint.
  Piezo Speaker - PC Mount: This is a small 12mm round speaker that operates around the audible 2kHz range. You can use these speakers to create simple music or user interfaces. Each speaker is PTH solderable and requires an operating voltage of 3.5-5V with a mean current of 35mA max. These speakers also have a typical sound output of 95 dBA and a coil resistance of 42 ±6.3 ohms.
  DIP - 4 pins: A DIP stand-in part for whatever IC you want. With 4 pins on a 300mil dual inline package (DIP) footprint.
  OLED 0.96" 128x64 I2C SSD1306 (GND/VCC): OLED 0.96" 128x64 I2C SSD1306 Pinout: GND/VCC/SCL/SDA
